# Fritzing sketch Untitled Sketch (saved by Fritzing 0.9.3b)
breadboards: 1

parts:
  Част1 = Arduino Uno (Rev3)
  IC1 = ULN2003A [package="DIP16 [THT]"]
  M1 = Stepper Motor - Unipolar
  V1 = DC Power [voltage=5]
  R1 = Trimmer Potentiometer [maximum_resistance=10kΩ package=THT]

nets:
  N1: Част1.D8, IC1.In_1
  N2: Част1.D9_PWM, IC1.In_2
  N3: Част1.D10_PWM/SS, IC1.In_3
  N4: Част1.D11_PWM/MOSI, IC1.In_4
  N5: Част1.GND, V1.V-, R1.leg1
  N6: Част1.A5/SCL, R1.wiper
  N7: Част1.5V, R1.leg2
  N8: IC1.Out_4, M1.D
  N9: IC1.Out_3, M1.C
  N10: IC1.Out_2, M1.B
  N11: IC1.Out_1, M1.A
  N12: M1.COMMON_1, M1.COMMON_2, V1.V+
